// Logisim project processor_riscv_evolution.circ as structural Verilog: 6 circuits, main circuit main
module main (
);

  ALU alu_1 ();  // open: B, A, F, Y, Zero
endmodule

module ALU (
  input  [2:0] F,
  input  [31:0] B,
  input  [31:0] A,
  output [31:0] Y,
  output Zero
);

  wire comparator_1_lt;
  wire [31:0] adder_1_out, and_1_out, bit_extender_1_out, multiplexer_1_out, not_1_out, or_1_out;

  assign not_1_out = ~B;  // NOT_Gate not_1, 32 bits wide
  Multiplexer #(.width(32)) multiplexer_1 (.in0(B), .in1(not_1_out), .out(multiplexer_1_out), .sel(F[0]));
  assign and_1_out = A & B;  // AND_Gate and_1, 32 bits wide
  assign or_1_out = A | B;  // OR_Gate or_1, 32 bits wide
  Comparator #(.mode("unsigned"), .width(32)) comparator_1 (.a(A), .b(B), .lt(comparator_1_lt));  // open: gt, eq
  Adder #(.width(32)) adder_1 (.a(multiplexer_1_out), .b(A), .out(adder_1_out), .cin(F[0]));  // open: cout
  assign bit_extender_1_out = {{31{comparator_1_lt}}, comparator_1_lt};  // Bit_Extender bit_extender_1
  Multiplexer #(.select(3), .width(32)) multiplexer_2 (
    .in0(adder_1_out), .in1(adder_1_out), .in2(and_1_out), .in3(or_1_out), .in5(bit_extender_1_out), .out(Y),
    .sel(F));  // open: in4, in6, in7
  Comparator #(.mode("unsigned"), .width(32)) comparator_2 (.a(Y), .b({32{1'b0}}), .eq(Zero));  // open: gt, lt
endmodule

module Datapath (
  input  in_1,
  output [2:0] A1_RS1,
  output [2:0] A2_RS2,
  output [2:0] A3_RD,
  output [7:0] out_5,
  output [31:0] t2,
  output [31:0] out_7,
  output [31:0] ROM_out,
  output [7:0] out_9,
  output [7:0] out_10
);

  wire alu_1_zero, and_1_out, clock_1_out, controlunit_1_alusrc, controlunit_1_branch, controlunit_1_regwrite;
  wire [2:0] controlunit_1_alucontrol;
  wire [7:0] adder_1_out, bitselector_1_out, multiplexer_1_out, PC_q;
  wire [31:0] alu_1_y, multiplexer_3_out, registerfile_1_rd1, registerfile_1_rd2;

  Clock clock_1 (.out(clock_1_out));
  Multiplexer #(.width(8)) multiplexer_1 (.in0(out_9), .in1(8'h14), .out(multiplexer_1_out), .sel(in_1));
  Register PC (.D(multiplexer_1_out), .en(1'b1), .clk(clock_1_out), .Q(PC_q));  // open: clr
  Multiplexer #(.width(8)) multiplexer_2 (.in0(adder_1_out), .in1(out_10), .out(out_9), .sel(and_1_out));
  Shifter #(.shift("lr")) shifter_1 (.in(PC_q), .\dist (3'b010), .out(out_5));
  Adder adder_1 (.a(8'h4), .b(PC_q), .out(adder_1_out));  // open: cin, cout
  ROM #(.dataWidth(32)) rom_1 (
    .addr(out_5), .data({ROM_out[31:23], A2_RS2, ROM_out[19:18], A1_RS1, ROM_out[14:10], A3_RD, ROM_out[6:0]}));
  BitSelector #(.group(8), .width(13)) bitselector_1 (
    .in({ROM_out[31], A3_RD[0], ROM_out[30:25], ROM_out[11:10], A3_RD[2:1], 1'b0}), .out(bitselector_1_out),
    .sel(1'b0));
  Adder adder_2 (.a(bitselector_1_out), .b(PC_q), .out(out_10));  // open: cin, cout
  assign out_7 = {{20{ROM_out[31]}}, {ROM_out[31:23], A2_RS2}};  // Bit_Extender bit_extender_1
  RegisterFile registerfile_1 (
    .WD3(alu_1_y), .CLK(clock_1_out), .A2(A2_RS2), .A1(A1_RS1), .A3(A3_RD), .WE3(controlunit_1_regwrite),
    .T2(t2), .RD1(registerfile_1_rd1), .RD2(registerfile_1_rd2));
  Multiplexer #(.width(32)) multiplexer_3 (
    .in0(registerfile_1_rd2), .in1(out_7), .out(multiplexer_3_out), .sel(controlunit_1_alusrc));
  ControlUnit controlunit_1 (
    .Instruction({ROM_out[31:23], A2_RS2, ROM_out[19:18], A1_RS1, ROM_out[14:10], A3_RD, ROM_out[6:0]}),
    .RegWrite(controlunit_1_regwrite), .ALUSrc(controlunit_1_alusrc), .ALUControl(controlunit_1_alucontrol),
    .Branch(controlunit_1_branch));
  ALU alu_1 (
    .B(multiplexer_3_out), .A(registerfile_1_rd1), .F(controlunit_1_alucontrol), .Y(alu_1_y),
    .Zero(alu_1_zero));
  and and_1 (and_1_out, controlunit_1_branch, alu_1_zero);

  assign {ROM_out[22:20], ROM_out[17:15], ROM_out[9:7]} = {A2_RS2, A1_RS1, A3_RD};

  // Notes on the sheet:
  //   PC + 4
  //   BTA = PC + imm
  //   contents of rom_1 (hex, n*v repeats v):
  //   400293 228393 5383b3 538663 ffd38393 fe000ce3 33
endmodule

module RegisterFile (
  input  CLK,
  input  [2:0] A1,
  input  [31:0] WD3,
  input  [2:0] A2,
  input  WE3,
  input  [2:0] A3,
  output [31:0] RD1,
  output [31:0] RD2,
  output [31:0] T2
);

  wire and_1_out, and_2_out, and_3_out, and_4_out, and_5_out, and_6_out, and_7_out, decoder_1_out0,
       decoder_1_out1, decoder_1_out2, decoder_1_out3, decoder_1_out4, decoder_1_out5, decoder_1_out6,
       decoder_1_out7;
  wire [31:0] register_1_q, register_2_q, register_3_q, register_4_q, register_5_q, register_6_q,
       register_7_q;

  Decoder #(.select(3)) decoder_1 (
    .out0(decoder_1_out0), .out1(decoder_1_out1), .out2(decoder_1_out2), .out3(decoder_1_out3),
    .out4(decoder_1_out4), .out5(decoder_1_out5), .out6(decoder_1_out6), .out7(decoder_1_out7), .sel(A3));  // open: en
  and and_1 (and_1_out, WE3, decoder_1_out1);
  and and_2 (and_2_out, WE3, decoder_1_out2);
  and and_3 (and_3_out, WE3, decoder_1_out3);
  and and_4 (and_4_out, WE3, decoder_1_out4);
  and and_5 (and_5_out, WE3, decoder_1_out5);
  and and_6 (and_6_out, WE3, decoder_1_out6);
  and and_7 (and_7_out, WE3, decoder_1_out7);
  Register #(.width(32)) register_1 (.D({32{1'b0}}), .en(CLK), .clk(decoder_1_out0), .Q(register_1_q));  // open: clr
  Register #(.width(32)) register_2 (.D(WD3), .en(and_1_out), .clk(CLK), .Q(register_2_q));  // open: clr
  Register #(.width(32)) register_3 (.D(WD3), .en(and_2_out), .clk(CLK), .Q(register_3_q));  // open: clr
  Register #(.width(32)) register_4 (.D(WD3), .en(and_3_out), .clk(CLK), .Q(register_4_q));  // open: clr
  Register #(.width(32)) register_5 (.D(WD3), .en(and_4_out), .clk(CLK), .Q(register_5_q));  // open: clr
  Register #(.width(32)) register_6 (.D(WD3), .en(and_5_out), .clk(CLK), .Q(register_6_q));  // open: clr
  Register #(.width(32)) register_7 (.D(WD3), .en(and_6_out), .clk(CLK), .Q(register_7_q));  // open: clr
  Register #(.width(32)) register_8 (.D(WD3), .en(and_7_out), .clk(CLK), .Q(T2));  // open: clr
  Multiplexer #(.enable("true"), .select(3), .width(32)) multiplexer_1 (
    .in0(register_1_q), .in1(register_2_q), .in2(register_3_q), .in3(register_4_q), .in4(register_5_q),
    .in5(register_6_q), .in6(register_7_q), .in7(T2), .out(RD1), .sel(A1));  // open: en
  Multiplexer #(.enable("true"), .select(3), .width(32)) multiplexer_2 (
    .in0(register_1_q), .in1(register_2_q), .in2(register_3_q), .in3(register_4_q), .in4(register_5_q),
    .in5(register_6_q), .in6(register_7_q), .in7(T2), .out(RD2), .sel(A2));  // open: en

  // Notes on the sheet:
  //   ra
  //   sp
  //   gp
  //   tp
  //   t0
  //   t1
  //   t2
  //   Zero
endmodule

module ControlUnit (
  input  [31:0] Instruction,
  output RegWrite,
  output ALUSrc,
  output [2:0] ALUControl,
  output Branch
);

  wire comparator_3_eq;

  Comparator #(.mode("unsigned"), .width(7)) comparator_1 (
    .a(Instruction[6:0]), .b(7'b1100011), .eq(Branch));  // open: gt, lt
  Comparator #(.mode("unsigned"), .width(7)) comparator_2 (
    .a(Instruction[6:0]), .b(7'b0010011), .eq(ALUSrc));  // open: gt, lt
  Comparator #(.mode("unsigned"), .width(7)) comparator_3 (
    .a(Instruction[6:0]), .b(7'b0110011), .eq(comparator_3_eq));  // open: gt, lt
  or or_1 (RegWrite, ALUSrc, comparator_3_eq);
  assign ALUControl = {{2{1'b0}}, Branch};  // Bit_Extender bit_extender_1

  // Notes on the sheet:
  //   beq
  //   addi
  //   add
endmodule

module Tests (
  output [31:0] Y,
  output [3:0] out_2,
  output [7:0] out_3
);


  assign out_2 = 4'b0010;
  assign out_3 = 8'h22;
  assign Y = 32'hf4010207;

  // Notes on the sheet:
  //   binary values in Logisim. Convince yourself how the bits are displayed.
  //   Example 1: A simple example that illustrates how 32-bit values are displayed as 
  //   Example 2) An example of how to extra certain bits from a (in this case) 32-bit wire. Here we extract the bits 8..11 from the 32-bit wire.
  //   Example 3) Sometimes it is useful to extra bits from different position and the re-assemble them. In this case, we extract bits 8..11 and bits 15..18 and assemble them into an 8-bit wire.
endmodule
